// Digital circuit GFX.dig as structural Verilog
module GFX (
  input  [27:0] gcore_interconnect,
  input  gcore_clk,
  input  in_6,
  input  gcore_assigned,
  input  in_8,
  output [63:0] r_data,
  output [6:0] c_data,
  output gcore_ready
);

  wire and_1_out, and_2_out, and_4_out, and_6_out, and_8_out, delay_1_out, delay_2_out, delay_3_out,
       rs_ff_as_2_q, rs_ff_as_3_q, rs_ff_as_4_q, rs_ff_as_5_q, rs_ff_as_19_q, rs_ff_as_20_q, rs_ff_as_21_q,
       rs_ff_as_22_q, rs_ff_as_23_q, rs_ff_as_24_q;
  wire [1:0] and_3_out;
  wire [1:1] rs_ff_as_1_q;
  wire [6:0] rs_ff_as_25_q;
  wire [25:0] and_10_out;
  wire [30:0] and_44_out;
  wire [32:0] and_11_out;
  wire [63:63] and_5_out;

  Delay delay_1 (.in(gcore_assigned), .out(delay_1_out));
  and and_1 (and_1_out, gcore_assigned, ~delay_1_out);  // And
  Delay delay_2 (.in(in_6), .out(delay_2_out));
  and and_2 (and_2_out, in_6, ~delay_2_out);  // And
  LedMatrix #(.colAddrBits(7), .rowDataBits(64)) Main_Monitor (.rows(r_data), .column(c_data));
  RS_FF_AS rs_ff_as_1 (.S(gcore_assigned), .R(and_2_out), .Q(rs_ff_as_1_q[1]));  // open: nQ
  assign and_3_out = gcore_interconnect[1:0] & {2{rs_ff_as_1_q[1]}};  // And and_3, 2 bits wide
  RS_FF_AS rs_ff_as_2 (.S(and_3_out[0]), .R(and_1_out), .Q(rs_ff_as_2_q));  // open: nQ
  RS_FF_AS rs_ff_as_3 (.S(and_3_out[1]), .R(and_1_out), .Q(rs_ff_as_3_q));  // open: nQ
  and and_4 (and_4_out, ~rs_ff_as_3_q, ~rs_ff_as_2_q);  // And
  and and_5 (and_5_out[63], ~rs_ff_as_3_q, rs_ff_as_2_q);  // And
  and and_6 (and_6_out, rs_ff_as_3_q, ~rs_ff_as_2_q);  // And
  // And and_7 has open pins: In_1=rs_ff_as_3_q, In_2=rs_ff_as_2_q, out=open
  LED led_1 (.in(and_4_out));
  Delay delay_3 (.in(and_5_out[63]), .out(delay_3_out));
  and and_8 (and_8_out, and_5_out[63], ~delay_3_out);  // And
  RS_FF_AS rs_ff_as_4 (.S(and_8_out), .R(and_1_out), .Q(rs_ff_as_4_q));  // open: nQ
  RS_FF_AS rs_ff_as_5 (.S(in_8), .R(and_1_out), .Q(rs_ff_as_5_q));  // open: nQ
  and and_9 (in_6, rs_ff_as_4_q, rs_ff_as_5_q);
  GraphicCard #(.graphicHeight(200), .graphicWidth(320)) graphiccard_1 ();  // open: A, str, C, ld, B, D
  assign and_10_out = gcore_interconnect[27:2] & {26{rs_ff_as_1_q[1]}};  // And and_10, 26 bits wide
  RS_FF_AS rs_ff_as_6 (.S(and_10_out[25]), .R(and_1_out));  // open: Q, nQ
  RS_FF_AS rs_ff_as_7 (.S(and_10_out[24]), .R(and_1_out));  // open: Q, nQ
  RS_FF_AS rs_ff_as_8 (.S(and_10_out[23]), .R(and_1_out));  // open: Q, nQ
  RS_FF_AS rs_ff_as_9 (.S(and_10_out[22]), .R(and_1_out));  // open: Q, nQ
  RS_FF_AS rs_ff_as_10 (.S(and_10_out[21]), .R(and_1_out));  // open: Q, nQ
  RS_FF_AS rs_ff_as_11 (.S(and_10_out[20]), .R(and_1_out));  // open: Q, nQ
  RS_FF_AS rs_ff_as_12 (.S(and_10_out[19]), .R(and_1_out));  // open: Q, nQ
  RS_FF_AS rs_ff_as_13 (.S(and_10_out[18]), .R(and_1_out));  // open: Q, nQ
  RS_FF_AS rs_ff_as_14 (.S(and_10_out[17]), .R(and_1_out));  // open: Q, nQ
  RS_FF_AS rs_ff_as_15 (.S(and_10_out[16]), .R(and_1_out));  // open: Q, nQ
  RS_FF_AS rs_ff_as_16 (.S(and_10_out[15]), .R(and_1_out));  // open: Q, nQ
  RS_FF_AS rs_ff_as_17 (.S(and_10_out[14]), .R(and_1_out));  // open: Q, nQ
  RS_FF_AS rs_ff_as_18 (.S(and_10_out[13]), .R(and_1_out));  // open: Q, nQ
  RS_FF_AS rs_ff_as_19 (.S(and_10_out[12]), .R(and_1_out), .Q(rs_ff_as_19_q));  // open: nQ
  RS_FF_AS rs_ff_as_20 (.S(and_10_out[11]), .R(and_1_out), .Q(rs_ff_as_20_q));  // open: nQ
  RS_FF_AS rs_ff_as_21 (.S(and_10_out[10]), .R(and_1_out), .Q(rs_ff_as_21_q));  // open: nQ
  RS_FF_AS rs_ff_as_22 (.S(and_10_out[9]), .R(and_1_out), .Q(rs_ff_as_22_q));  // open: nQ
  RS_FF_AS rs_ff_as_23 (.S(and_10_out[8]), .R(and_1_out), .Q(rs_ff_as_23_q));  // open: nQ
  RS_FF_AS rs_ff_as_24 (.S(and_10_out[7]), .R(and_1_out), .Q(rs_ff_as_24_q));  // open: nQ
  RS_FF_AS rs_ff_as_25 (.S(and_10_out[6]), .R(and_1_out), .Q(rs_ff_as_25_q[6]));  // open: nQ
  RS_FF_AS rs_ff_as_26 (.S(and_10_out[5]), .R(and_1_out), .Q(rs_ff_as_25_q[5]));  // open: nQ
  RS_FF_AS rs_ff_as_27 (.S(and_10_out[4]), .R(and_1_out), .Q(rs_ff_as_25_q[4]));  // open: nQ
  RS_FF_AS rs_ff_as_28 (.S(and_10_out[3]), .R(and_1_out), .Q(rs_ff_as_25_q[3]));  // open: nQ
  RS_FF_AS rs_ff_as_29 (.S(and_10_out[2]), .R(and_1_out), .Q(rs_ff_as_25_q[2]));  // open: nQ
  RS_FF_AS rs_ff_as_30 (.S(and_10_out[1]), .R(and_1_out), .Q(rs_ff_as_25_q[1]));  // open: nQ
  RS_FF_AS rs_ff_as_31 (.S(and_10_out[0]), .R(and_1_out), .Q(rs_ff_as_25_q[0]));  // open: nQ
  and and_11 (and_11_out[0], ~rs_ff_as_19_q, ~rs_ff_as_20_q, ~rs_ff_as_21_q, ~rs_ff_as_22_q, ~rs_ff_as_23_q, ~rs_ff_as_24_q);  // And
  and and_12 (and_11_out[1], ~rs_ff_as_19_q, ~rs_ff_as_20_q, ~rs_ff_as_21_q, ~rs_ff_as_22_q, ~rs_ff_as_23_q, rs_ff_as_24_q);  // And
  and and_13 (and_11_out[2], ~rs_ff_as_19_q, ~rs_ff_as_20_q, ~rs_ff_as_21_q, ~rs_ff_as_22_q, rs_ff_as_23_q, ~rs_ff_as_24_q);  // And
  and and_14 (and_11_out[3], ~rs_ff_as_19_q, ~rs_ff_as_20_q, ~rs_ff_as_21_q, ~rs_ff_as_22_q, rs_ff_as_23_q, rs_ff_as_24_q);  // And
  and and_15 (and_11_out[4], ~rs_ff_as_19_q, ~rs_ff_as_20_q, ~rs_ff_as_21_q, rs_ff_as_22_q, ~rs_ff_as_23_q, ~rs_ff_as_24_q);  // And
  and and_16 (and_11_out[5], ~rs_ff_as_19_q, ~rs_ff_as_20_q, ~rs_ff_as_21_q, rs_ff_as_22_q, ~rs_ff_as_23_q, rs_ff_as_24_q);  // And
  and and_17 (and_11_out[6], ~rs_ff_as_19_q, ~rs_ff_as_20_q, ~rs_ff_as_21_q, rs_ff_as_22_q, rs_ff_as_23_q, ~rs_ff_as_24_q);  // And
  and and_18 (and_11_out[7], ~rs_ff_as_19_q, ~rs_ff_as_20_q, ~rs_ff_as_21_q, rs_ff_as_22_q, rs_ff_as_23_q, rs_ff_as_24_q);  // And
  and and_19 (and_11_out[8], ~rs_ff_as_19_q, ~rs_ff_as_20_q, rs_ff_as_21_q, ~rs_ff_as_22_q, ~rs_ff_as_23_q, ~rs_ff_as_24_q);  // And
  and and_20 (and_11_out[9], ~rs_ff_as_19_q, ~rs_ff_as_20_q, rs_ff_as_21_q, ~rs_ff_as_22_q, ~rs_ff_as_23_q, rs_ff_as_24_q);  // And
  and and_21 (and_11_out[10], ~rs_ff_as_19_q, ~rs_ff_as_20_q, rs_ff_as_21_q, ~rs_ff_as_22_q, rs_ff_as_23_q, ~rs_ff_as_24_q);  // And
  and and_22 (and_11_out[11], ~rs_ff_as_19_q, ~rs_ff_as_20_q, rs_ff_as_21_q, ~rs_ff_as_22_q, rs_ff_as_23_q, rs_ff_as_24_q);  // And
  and and_23 (and_11_out[12], ~rs_ff_as_19_q, ~rs_ff_as_20_q, rs_ff_as_21_q, rs_ff_as_22_q, ~rs_ff_as_23_q, ~rs_ff_as_24_q);  // And
  and and_24 (and_11_out[13], ~rs_ff_as_19_q, ~rs_ff_as_20_q, rs_ff_as_21_q, rs_ff_as_22_q, ~rs_ff_as_23_q, rs_ff_as_24_q);  // And
  and and_25 (and_11_out[14], ~rs_ff_as_19_q, ~rs_ff_as_20_q, rs_ff_as_21_q, rs_ff_as_22_q, rs_ff_as_23_q, ~rs_ff_as_24_q);  // And
  and and_26 (and_11_out[15], ~rs_ff_as_19_q, ~rs_ff_as_20_q, rs_ff_as_21_q, rs_ff_as_22_q, rs_ff_as_23_q, rs_ff_as_24_q);  // And
  and and_27 (and_11_out[16], ~rs_ff_as_19_q, rs_ff_as_20_q, ~rs_ff_as_21_q, ~rs_ff_as_22_q, ~rs_ff_as_23_q, ~rs_ff_as_24_q);  // And
  and and_28 (and_11_out[17], ~rs_ff_as_19_q, rs_ff_as_20_q, ~rs_ff_as_21_q, ~rs_ff_as_22_q, ~rs_ff_as_23_q, rs_ff_as_24_q);  // And
  and and_29 (and_11_out[18], ~rs_ff_as_19_q, rs_ff_as_20_q, ~rs_ff_as_21_q, ~rs_ff_as_22_q, rs_ff_as_23_q, ~rs_ff_as_24_q);  // And
  and and_30 (and_11_out[19], ~rs_ff_as_19_q, rs_ff_as_20_q, ~rs_ff_as_21_q, ~rs_ff_as_22_q, rs_ff_as_23_q, rs_ff_as_24_q);  // And
  and and_31 (and_11_out[20], ~rs_ff_as_19_q, rs_ff_as_20_q, ~rs_ff_as_21_q, rs_ff_as_22_q, ~rs_ff_as_23_q, ~rs_ff_as_24_q);  // And
  and and_32 (and_11_out[21], ~rs_ff_as_19_q, rs_ff_as_20_q, ~rs_ff_as_21_q, rs_ff_as_22_q, ~rs_ff_as_23_q, rs_ff_as_24_q);  // And
  and and_33 (and_11_out[22], ~rs_ff_as_19_q, rs_ff_as_20_q, ~rs_ff_as_21_q, rs_ff_as_22_q, rs_ff_as_23_q, ~rs_ff_as_24_q);  // And
  and and_34 (and_11_out[23], ~rs_ff_as_19_q, rs_ff_as_20_q, ~rs_ff_as_21_q, rs_ff_as_22_q, rs_ff_as_23_q, rs_ff_as_24_q);  // And
  and and_35 (and_11_out[24], ~rs_ff_as_19_q, rs_ff_as_20_q, rs_ff_as_21_q, ~rs_ff_as_22_q, ~rs_ff_as_23_q, ~rs_ff_as_24_q);  // And
  and and_36 (and_11_out[25], ~rs_ff_as_19_q, rs_ff_as_20_q, rs_ff_as_21_q, ~rs_ff_as_22_q, ~rs_ff_as_23_q, rs_ff_as_24_q);  // And
  and and_37 (and_11_out[26], ~rs_ff_as_19_q, rs_ff_as_20_q, rs_ff_as_21_q, ~rs_ff_as_22_q, rs_ff_as_23_q, ~rs_ff_as_24_q);  // And
  and and_38 (and_11_out[27], ~rs_ff_as_19_q, rs_ff_as_20_q, rs_ff_as_21_q, ~rs_ff_as_22_q, rs_ff_as_23_q, rs_ff_as_24_q);  // And
  and and_39 (and_11_out[28], ~rs_ff_as_19_q, rs_ff_as_20_q, rs_ff_as_21_q, rs_ff_as_22_q, ~rs_ff_as_23_q, ~rs_ff_as_24_q);  // And
  and and_40 (and_11_out[29], ~rs_ff_as_19_q, rs_ff_as_20_q, rs_ff_as_21_q, rs_ff_as_22_q, ~rs_ff_as_23_q, rs_ff_as_24_q);  // And
  and and_41 (and_11_out[30], ~rs_ff_as_19_q, rs_ff_as_20_q, rs_ff_as_21_q, rs_ff_as_22_q, rs_ff_as_23_q, ~rs_ff_as_24_q);  // And
  and and_42 (and_11_out[31], ~rs_ff_as_19_q, rs_ff_as_20_q, rs_ff_as_21_q, rs_ff_as_22_q, rs_ff_as_23_q, rs_ff_as_24_q);  // And
  and and_43 (and_11_out[32], rs_ff_as_19_q, ~rs_ff_as_20_q, ~rs_ff_as_21_q, ~rs_ff_as_22_q, ~rs_ff_as_23_q, ~rs_ff_as_24_q);  // And
  and and_44 (and_44_out[0], rs_ff_as_19_q, ~rs_ff_as_20_q, ~rs_ff_as_21_q, ~rs_ff_as_22_q, ~rs_ff_as_23_q, rs_ff_as_24_q);  // And
  and and_45 (and_44_out[1], rs_ff_as_19_q, ~rs_ff_as_20_q, ~rs_ff_as_21_q, ~rs_ff_as_22_q, rs_ff_as_23_q, ~rs_ff_as_24_q);  // And
  and and_46 (and_44_out[2], rs_ff_as_19_q, ~rs_ff_as_20_q, ~rs_ff_as_21_q, ~rs_ff_as_22_q, rs_ff_as_23_q, rs_ff_as_24_q);  // And
  and and_47 (and_44_out[3], rs_ff_as_19_q, ~rs_ff_as_20_q, ~rs_ff_as_21_q, rs_ff_as_22_q, ~rs_ff_as_23_q, ~rs_ff_as_24_q);  // And
  and and_48 (and_44_out[4], rs_ff_as_19_q, ~rs_ff_as_20_q, ~rs_ff_as_21_q, rs_ff_as_22_q, ~rs_ff_as_23_q, rs_ff_as_24_q);  // And
  and and_49 (and_44_out[5], rs_ff_as_19_q, ~rs_ff_as_20_q, ~rs_ff_as_21_q, rs_ff_as_22_q, rs_ff_as_23_q, ~rs_ff_as_24_q);  // And
  and and_50 (and_44_out[6], rs_ff_as_19_q, ~rs_ff_as_20_q, ~rs_ff_as_21_q, rs_ff_as_22_q, rs_ff_as_23_q, rs_ff_as_24_q);  // And
  and and_51 (and_44_out[7], rs_ff_as_19_q, ~rs_ff_as_20_q, rs_ff_as_21_q, ~rs_ff_as_22_q, ~rs_ff_as_23_q, ~rs_ff_as_24_q);  // And
  and and_52 (and_44_out[8], rs_ff_as_19_q, ~rs_ff_as_20_q, rs_ff_as_21_q, ~rs_ff_as_22_q, ~rs_ff_as_23_q, rs_ff_as_24_q);  // And
  and and_53 (and_44_out[9], rs_ff_as_19_q, ~rs_ff_as_20_q, rs_ff_as_21_q, ~rs_ff_as_22_q, rs_ff_as_23_q, ~rs_ff_as_24_q);  // And
  and and_54 (and_44_out[10], rs_ff_as_19_q, ~rs_ff_as_20_q, rs_ff_as_21_q, ~rs_ff_as_22_q, rs_ff_as_23_q, rs_ff_as_24_q);  // And
  and and_55 (and_44_out[11], rs_ff_as_19_q, ~rs_ff_as_20_q, rs_ff_as_21_q, rs_ff_as_22_q, ~rs_ff_as_23_q, ~rs_ff_as_24_q);  // And
  and and_56 (and_44_out[12], rs_ff_as_19_q, ~rs_ff_as_20_q, rs_ff_as_21_q, rs_ff_as_22_q, ~rs_ff_as_23_q, rs_ff_as_24_q);  // And
  and and_57 (and_44_out[13], rs_ff_as_19_q, ~rs_ff_as_20_q, rs_ff_as_21_q, rs_ff_as_22_q, rs_ff_as_23_q, ~rs_ff_as_24_q);  // And
  and and_58 (and_44_out[14], rs_ff_as_19_q, ~rs_ff_as_20_q, rs_ff_as_21_q, rs_ff_as_22_q, rs_ff_as_23_q, rs_ff_as_24_q);  // And
  and and_59 (and_44_out[15], rs_ff_as_19_q, rs_ff_as_20_q, ~rs_ff_as_21_q, ~rs_ff_as_22_q, ~rs_ff_as_23_q, ~rs_ff_as_24_q);  // And
  and and_60 (and_44_out[16], rs_ff_as_19_q, rs_ff_as_20_q, ~rs_ff_as_21_q, ~rs_ff_as_22_q, ~rs_ff_as_23_q, rs_ff_as_24_q);  // And
  and and_61 (and_44_out[17], rs_ff_as_19_q, rs_ff_as_20_q, ~rs_ff_as_21_q, ~rs_ff_as_22_q, rs_ff_as_23_q, ~rs_ff_as_24_q);  // And
  and and_62 (and_44_out[18], rs_ff_as_19_q, rs_ff_as_20_q, ~rs_ff_as_21_q, ~rs_ff_as_22_q, rs_ff_as_23_q, rs_ff_as_24_q);  // And
  and and_63 (and_44_out[19], rs_ff_as_19_q, rs_ff_as_20_q, ~rs_ff_as_21_q, rs_ff_as_22_q, ~rs_ff_as_23_q, ~rs_ff_as_24_q);  // And
  and and_64 (and_44_out[20], rs_ff_as_19_q, rs_ff_as_20_q, ~rs_ff_as_21_q, rs_ff_as_22_q, ~rs_ff_as_23_q, rs_ff_as_24_q);  // And
  and and_65 (and_44_out[21], rs_ff_as_19_q, rs_ff_as_20_q, ~rs_ff_as_21_q, rs_ff_as_22_q, rs_ff_as_23_q, ~rs_ff_as_24_q);  // And
  and and_66 (and_44_out[22], rs_ff_as_19_q, rs_ff_as_20_q, ~rs_ff_as_21_q, rs_ff_as_22_q, rs_ff_as_23_q, rs_ff_as_24_q);  // And
  and and_67 (and_44_out[23], rs_ff_as_19_q, rs_ff_as_20_q, rs_ff_as_21_q, ~rs_ff_as_22_q, ~rs_ff_as_23_q, ~rs_ff_as_24_q);  // And
  and and_68 (and_44_out[24], rs_ff_as_19_q, rs_ff_as_20_q, rs_ff_as_21_q, ~rs_ff_as_22_q, ~rs_ff_as_23_q, rs_ff_as_24_q);  // And
  and and_69 (and_44_out[25], rs_ff_as_19_q, rs_ff_as_20_q, rs_ff_as_21_q, ~rs_ff_as_22_q, rs_ff_as_23_q, ~rs_ff_as_24_q);  // And
  and and_70 (and_44_out[26], rs_ff_as_19_q, rs_ff_as_20_q, rs_ff_as_21_q, ~rs_ff_as_22_q, rs_ff_as_23_q, rs_ff_as_24_q);  // And
  and and_71 (and_44_out[27], rs_ff_as_19_q, rs_ff_as_20_q, rs_ff_as_21_q, rs_ff_as_22_q, ~rs_ff_as_23_q, ~rs_ff_as_24_q);  // And
  and and_72 (and_44_out[28], rs_ff_as_19_q, rs_ff_as_20_q, rs_ff_as_21_q, rs_ff_as_22_q, ~rs_ff_as_23_q, rs_ff_as_24_q);  // And
  and and_73 (and_44_out[29], rs_ff_as_19_q, rs_ff_as_20_q, rs_ff_as_21_q, rs_ff_as_22_q, rs_ff_as_23_q, ~rs_ff_as_24_q);  // And
  and and_74 (and_44_out[30], rs_ff_as_19_q, rs_ff_as_20_q, rs_ff_as_21_q, rs_ff_as_22_q, rs_ff_as_23_q, rs_ff_as_24_q);
  assign c_data = {7{and_5_out[63]}} & rs_ff_as_25_q;  // And and_75, 7 bits wide
  assign r_data = {64{and_5_out[63]}} & {and_44_out, and_11_out};  // And and_76, 64 bits wide

  assign gcore_ready = in_6;

  // Notes on the sheet:
  //   gcore_clk: Hz: 500
  //   draw-point
  //   draw-line
  //   MSB
endmodule
