// Digital circuit gcore.dig as structural Verilog
module gcore (
  input  [31:0] gcore_interconnect,
  input  gcore_assigned,
  input  gclk,
  output [14:0] framebuffer_addr,
  output gcore_ready
);

  wire and_1_out, and_2_out, and_4_out, and_6_out, and_7_out, and_8_out, delay_1_out, delay_2_out,
       delay_3_out, delay_4_out, or_1_out, pulldown_1_out, rs_ff_as_2_q, rs_ff_as_3_q;
  wire [1:0] and_3_out;
  wire [1:1] rs_ff_as_1_q;
  wire [6:0] rs_ff_as_28_q;
  wire [7:0] rs_ff_as_20_q;
  wire [14:14] and_5_out;
  wire [29:0] and_9_out;

  Delay delay_1 (.in(gcore_assigned), .out(delay_1_out));
  and and_1 (and_1_out, gcore_assigned, ~delay_1_out);  // And
  Delay delay_2 (.in(gcore_ready), .out(delay_2_out));
  and and_2 (and_2_out, gcore_ready, ~delay_2_out);  // And
  RS_FF_AS rs_ff_as_1 (.S(gcore_assigned), .R(and_2_out), .Q(rs_ff_as_1_q[1]));  // open: nQ
  assign and_3_out = gcore_interconnect[31:30] & {2{rs_ff_as_1_q[1]}};  // And and_3, 2 bits wide
  RS_FF_AS rs_ff_as_2 (.S(and_3_out[0]), .R(and_1_out), .Q(rs_ff_as_2_q));  // open: nQ
  RS_FF_AS rs_ff_as_3 (.S(and_3_out[1]), .R(and_1_out), .Q(rs_ff_as_3_q));  // open: nQ
  and and_4 (and_4_out, ~rs_ff_as_3_q, ~rs_ff_as_2_q);  // And
  and and_5 (and_5_out[14], ~rs_ff_as_3_q, rs_ff_as_2_q);  // And
  and and_6 (and_6_out, rs_ff_as_3_q, ~rs_ff_as_2_q);  // And
  and and_7 (and_7_out, rs_ff_as_3_q, rs_ff_as_2_q);
  LED led_1 (.in(and_4_out));
  Delay delay_3 (.in(and_5_out[14]), .out(delay_3_out));
  and and_8 (and_8_out, and_5_out[14], ~delay_3_out);  // And
  Delay delay_4 (.in(and_8_out), .out(delay_4_out));
  PullDown pulldown_1 (.out(pulldown_1_out));
  or or_1 (or_1_out, delay_4_out, pulldown_1_out);
  RS_FF_AS #(.Default(1)) rs_ff_as_4 (.S(or_1_out), .R(and_1_out), .Q(gcore_ready));  // open: nQ
  assign and_9_out = gcore_interconnect[29:0] & {30{rs_ff_as_1_q[1]}};  // And and_9, 30 bits wide
  RS_FF_AS rs_ff_as_5 (.S(and_9_out[29]), .R(and_1_out));  // open: Q, nQ
  RS_FF_AS rs_ff_as_6 (.S(and_9_out[28]), .R(and_1_out));  // open: Q, nQ
  RS_FF_AS rs_ff_as_7 (.S(and_9_out[27]), .R(and_1_out));  // open: Q, nQ
  RS_FF_AS rs_ff_as_8 (.S(and_9_out[26]), .R(and_1_out));  // open: Q, nQ
  RS_FF_AS rs_ff_as_9 (.S(and_9_out[25]), .R(and_1_out));  // open: Q, nQ
  RS_FF_AS rs_ff_as_10 (.S(and_9_out[24]), .R(and_1_out));  // open: Q, nQ
  RS_FF_AS rs_ff_as_11 (.S(and_9_out[23]), .R(and_1_out));  // open: Q, nQ
  RS_FF_AS rs_ff_as_12 (.S(and_9_out[22]), .R(and_1_out));  // open: Q, nQ
  RS_FF_AS rs_ff_as_13 (.S(and_9_out[21]), .R(and_1_out));  // open: Q, nQ
  RS_FF_AS rs_ff_as_14 (.S(and_9_out[20]), .R(and_1_out));  // open: Q, nQ
  RS_FF_AS rs_ff_as_15 (.S(and_9_out[19]), .R(and_1_out));  // open: Q, nQ
  RS_FF_AS rs_ff_as_16 (.S(and_9_out[18]), .R(and_1_out));  // open: Q, nQ
  RS_FF_AS rs_ff_as_17 (.S(and_9_out[17]), .R(and_1_out));  // open: Q, nQ
  RS_FF_AS rs_ff_as_18 (.S(and_9_out[16]), .R(and_1_out));  // open: Q, nQ
  RS_FF_AS rs_ff_as_19 (.S(and_9_out[15]), .R(and_1_out));  // open: Q, nQ
  RS_FF_AS rs_ff_as_20 (.S(and_9_out[14]), .R(and_1_out), .Q(rs_ff_as_20_q[7]));  // open: nQ
  RS_FF_AS rs_ff_as_21 (.S(and_9_out[13]), .R(and_1_out), .Q(rs_ff_as_20_q[6]));  // open: nQ
  RS_FF_AS rs_ff_as_22 (.S(and_9_out[12]), .R(and_1_out), .Q(rs_ff_as_20_q[5]));  // open: nQ
  RS_FF_AS rs_ff_as_23 (.S(and_9_out[11]), .R(and_1_out), .Q(rs_ff_as_20_q[4]));  // open: nQ
  RS_FF_AS rs_ff_as_24 (.S(and_9_out[10]), .R(and_1_out), .Q(rs_ff_as_20_q[3]));  // open: nQ
  RS_FF_AS rs_ff_as_25 (.S(and_9_out[9]), .R(and_1_out), .Q(rs_ff_as_20_q[2]));  // open: nQ
  RS_FF_AS rs_ff_as_26 (.S(and_9_out[8]), .R(and_1_out), .Q(rs_ff_as_20_q[1]));  // open: nQ
  RS_FF_AS rs_ff_as_27 (.S(and_9_out[7]), .R(and_1_out), .Q(rs_ff_as_20_q[0]));  // open: nQ
  RS_FF_AS rs_ff_as_28 (.S(and_9_out[6]), .R(and_1_out), .Q(rs_ff_as_28_q[6]));  // open: nQ
  RS_FF_AS rs_ff_as_29 (.S(and_9_out[5]), .R(and_1_out), .Q(rs_ff_as_28_q[5]));  // open: nQ
  RS_FF_AS rs_ff_as_30 (.S(and_9_out[4]), .R(and_1_out), .Q(rs_ff_as_28_q[4]));  // open: nQ
  RS_FF_AS rs_ff_as_31 (.S(and_9_out[3]), .R(and_1_out), .Q(rs_ff_as_28_q[3]));  // open: nQ
  RS_FF_AS rs_ff_as_32 (.S(and_9_out[2]), .R(and_1_out), .Q(rs_ff_as_28_q[2]));  // open: nQ
  RS_FF_AS rs_ff_as_33 (.S(and_9_out[1]), .R(and_1_out), .Q(rs_ff_as_28_q[1]));  // open: nQ
  RS_FF_AS rs_ff_as_34 (.S(and_9_out[0]), .R(and_1_out), .Q(rs_ff_as_28_q[0]));  // open: nQ
  // And and_10 is placed but not wired
  assign framebuffer_addr = {15{and_5_out[14]}} & {rs_ff_as_28_q, rs_ff_as_20_q};  // And and_11, 15 bits wide

  // Notes on the sheet:
  //   draw-point
  //   draw-line
  //   MSB
endmodule
