// Digital circuit gpu.dig as structural Verilog
module gpu (
  input  gcore_clk,
  input  [14:0] gcore_data_in,
  input  [2:0] gcore_instr,
  output gcore_data_out,
  output [14:0] gcore_addr_out
);

  wire and_1_out, and_2_out, and_5_out, and_9_out, and_10_out, and_11_out, and_12_out, and_13_out,
       and_14_out, and_15_out, and_16_out, and_18_out, and_19_out, and_20_out, and_21_out, and_22_out,
       and_23_out, and_24_out, and_25_out, and_26_out, and_27_out, and_28_out, and_29_out, and_30_out,
       and_31_out, and_32_out, and_33_out, and_34_out, and_35_out, and_36_out, and_37_out, and_38_out,
       and_39_out, and_40_out, and_41_out, and_42_out, and_43_out, and_44_out, and_45_out, and_46_out,
       and_47_out, and_48_out, and_49_out, and_50_out, and_51_out, and_52_out, and_53_out, and_54_out,
       and_55_out, and_56_out, and_57_out, and_58_out, and_59_out, and_60_out, and_61_out, and_62_out,
       and_63_out, and_64_out, and_65_out, and_67_out, and_68_out, and_69_out, and_70_out, and_71_out,
       and_72_out, and_73_out, and_74_out, and_75_out, and_76_out, and_77_out, and_78_out, and_79_out,
       and_80_out, and_81_out, and_82_out, and_83_out, and_84_out, and_85_out, and_86_out, and_87_out,
       and_88_out, and_89_out, and_90_out, and_91_out, and_92_out, and_93_out, and_94_out, and_95_out,
       driver_1_out, jk_ff_1_q, jk_ff_2_q, jk_ff_3_q, jk_ff_4_q, jk_ff_5_q, jk_ff_6_q, rs_ff_1_q, rs_ff_2_q,
       rs_ff_3_q, rs_ff_4_q, rs_ff_5_q, rs_ff_6_q, rs_ff_7_q, rs_ff_8_q, rs_ff_9_q, rs_ff_10_q, rs_ff_11_q,
       rs_ff_12_q, rs_ff_13_q, rs_ff_14_q, rs_ff_15_q, rs_ff_16_q, rs_ff_32_q, rs_ff_33_q, rs_ff_34_q,
       rs_ff_35_q, rs_ff_36_q, rs_ff_37_q, rs_ff_38_q, rs_ff_39_q, rs_ff_40_q, rs_ff_41_q, rs_ff_42_q,
       rs_ff_43_q, rs_ff_44_q, rs_ff_45_q, rs_ff_46_q, rs_ff_47_q, rs_ff_48_q, rs_ff_49_q, rs_ff_50_q,
       rs_ff_51_q, rs_ff_52_q, rs_ff_53_q, rs_ff_54_q, rs_ff_55_q, rs_ff_56_q, rs_ff_57_q, rs_ff_58_q,
       rs_ff_59_q, rs_ff_60_q, rs_ff_61_q, rs_ff_62_q, rs_ff_63_q, rs_ff_64_q, rs_ff_65_q, rs_ff_66_q,
       rs_ff_67_q, rs_ff_68_q, rs_ff_69_q, rs_ff_70_q, rs_ff_71_q, rs_ff_72_q, rs_ff_73_q, rs_ff_74_q,
       rs_ff_75_q, rs_ff_76_q, rs_ff_77_q, rs_ff_78_q, rs_ff_79_q, rs_ff_as_1_q, undriven, undriven_2,
       undriven_3, undriven_4, undriven_5, undriven_6, undriven_7, undriven_8, undriven_9, undriven_10,
       undriven_11, undriven_12, undriven_13, undriven_14, undriven_15, undriven_16, undriven_17,
       undriven_18, undriven_19, undriven_20, undriven_21, undriven_22, undriven_23, undriven_24,
       undriven_25, undriven_26, undriven_27, undriven_28, undriven_29, undriven_30, undriven_31,
       undriven_32, undriven_33, undriven_34, undriven_35, undriven_36, undriven_37, undriven_38,
       undriven_39, undriven_40, undriven_41, undriven_42, undriven_43, undriven_44, undriven_45,
       undriven_46, undriven_47, undriven_48, undriven_49, undriven_50, undriven_51, undriven_52,
       undriven_53, undriven_54, undriven_55, undriven_56, undriven_57, undriven_58, undriven_59,
       undriven_60, undriven_61, undriven_62, undriven_63, undriven_64;
  wire [7:0] and_66_out;
  wire [7:7] and_4_out;
  wire [14:0] and_17_out, rs_ff_17_q;
  wire [14:14] and_3_out;

  and and_1 (and_1_out, ~gcore_instr[2], ~gcore_instr[1], ~gcore_instr[0]);  // And
  and and_2 (and_2_out, ~gcore_instr[2], ~gcore_instr[1], gcore_instr[0]);  // And
  and and_3 (and_3_out[14], ~gcore_instr[2], gcore_instr[1], ~gcore_instr[0]);  // And
  and and_4 (and_4_out[7], ~gcore_instr[2], gcore_instr[1], gcore_instr[0]);  // And
  and and_5 (and_5_out, gcore_instr[2], ~gcore_instr[1], ~gcore_instr[0]);  // And
  // And and_6 has open pins: In_1=gcore_instr[2], In_2=gcore_instr[1], In_3=gcore_instr[0], out=open
  // And and_7 has open pins: In_1=gcore_instr[2], In_2=gcore_instr[1], In_3=gcore_instr[0], out=open
  // And and_8 has open pins: In_1=gcore_instr[2], In_2=gcore_instr[1], In_3=gcore_instr[0], out=open
  LED led_1 (.in(and_1_out));
  and and_9 (and_9_out, and_50_out, and_66_out[7]);
  and and_10 (and_10_out, and_51_out, and_66_out[7]);
  and and_11 (and_11_out, and_52_out, and_66_out[7]);
  and and_12 (and_12_out, and_53_out, and_66_out[7]);
  and and_13 (and_13_out, and_54_out, and_66_out[7]);
  and and_14 (and_14_out, and_55_out, and_66_out[7]);
  and and_15 (and_15_out, and_56_out, and_66_out[7]);
  and and_16 (and_16_out, and_57_out, and_66_out[7]);
  RS_FF rs_ff_1 (.S(and_9_out), .C(gcore_clk), .R(and_2_out), .Q(rs_ff_1_q));  // open: nQ
  RS_FF rs_ff_2 (.S(and_10_out), .C(gcore_clk), .R(and_2_out), .Q(rs_ff_2_q));  // open: nQ
  RS_FF rs_ff_3 (.S(and_11_out), .C(gcore_clk), .R(and_2_out), .Q(rs_ff_3_q));  // open: nQ
  RS_FF rs_ff_4 (.S(and_12_out), .C(gcore_clk), .R(and_2_out), .Q(rs_ff_4_q));  // open: nQ
  RS_FF rs_ff_5 (.S(and_13_out), .C(gcore_clk), .R(and_2_out), .Q(rs_ff_5_q));  // open: nQ
  RS_FF rs_ff_6 (.S(and_14_out), .C(gcore_clk), .R(and_2_out), .Q(rs_ff_6_q));  // open: nQ
  RS_FF rs_ff_7 (.S(and_15_out), .C(gcore_clk), .R(and_2_out), .Q(rs_ff_7_q));  // open: nQ
  RS_FF rs_ff_8 (.S(and_16_out), .C(gcore_clk), .R(and_2_out), .Q(rs_ff_8_q));  // open: nQ
  LED led_2 (.in(rs_ff_1_q));
  LED led_3 (.in(rs_ff_2_q));
  LED led_4 (.in(rs_ff_3_q));
  LED led_5 (.in(rs_ff_4_q));
  LED led_6 (.in(rs_ff_5_q));
  LED led_7 (.in(rs_ff_6_q));
  LED led_8 (.in(rs_ff_7_q));
  LED led_9 (.in(rs_ff_8_q));
  assign driver_1_out = undriven_57 ? rs_ff_1_q : 1'bz;  // Driver driver_1
  assign driver_1_out = undriven_58 ? rs_ff_2_q : 1'bz;  // Driver driver_2
  assign driver_1_out = undriven_59 ? rs_ff_3_q : 1'bz;  // Driver driver_3
  assign driver_1_out = undriven_60 ? rs_ff_4_q : 1'bz;  // Driver driver_4
  assign driver_1_out = undriven_61 ? rs_ff_5_q : 1'bz;  // Driver driver_5
  assign driver_1_out = undriven_62 ? rs_ff_6_q : 1'bz;  // Driver driver_6
  assign driver_1_out = undriven_63 ? rs_ff_7_q : 1'bz;  // Driver driver_7
  assign driver_1_out = undriven_64 ? rs_ff_8_q : 1'bz;  // Driver driver_8
  PullDown pulldown_1 (.out(driver_1_out));
  assign and_17_out = gcore_data_in & {15{and_3_out[14]}};  // And and_17, 15 bits wide
  and and_18 (and_18_out, and_50_out, and_66_out[6]);
  and and_19 (and_19_out, and_51_out, and_66_out[6]);
  and and_20 (and_20_out, and_52_out, and_66_out[6]);
  and and_21 (and_21_out, and_53_out, and_66_out[6]);
  and and_22 (and_22_out, and_54_out, and_66_out[6]);
  and and_23 (and_23_out, and_55_out, and_66_out[6]);
  and and_24 (and_24_out, and_56_out, and_66_out[6]);
  and and_25 (and_25_out, and_57_out, and_66_out[6]);
  RS_FF rs_ff_9 (.S(and_18_out), .C(gcore_clk), .R(and_2_out), .Q(rs_ff_9_q));  // open: nQ
  RS_FF rs_ff_10 (.S(and_19_out), .C(gcore_clk), .R(and_2_out), .Q(rs_ff_10_q));  // open: nQ
  RS_FF rs_ff_11 (.S(and_20_out), .C(gcore_clk), .R(and_2_out), .Q(rs_ff_11_q));  // open: nQ
  RS_FF rs_ff_12 (.S(and_21_out), .C(gcore_clk), .R(and_2_out), .Q(rs_ff_12_q));  // open: nQ
  RS_FF rs_ff_13 (.S(and_22_out), .C(gcore_clk), .R(and_2_out), .Q(rs_ff_13_q));  // open: nQ
  RS_FF rs_ff_14 (.S(and_23_out), .C(gcore_clk), .R(and_2_out), .Q(rs_ff_14_q));  // open: nQ
  RS_FF rs_ff_15 (.S(and_24_out), .C(gcore_clk), .R(and_2_out), .Q(rs_ff_15_q));  // open: nQ
  RS_FF rs_ff_16 (.S(and_25_out), .C(gcore_clk), .R(and_2_out), .Q(rs_ff_16_q));  // open: nQ
  RS_FF rs_ff_17 (.S(and_17_out[0]), .C(gcore_clk), .R(and_2_out), .Q(rs_ff_17_q[0]));  // open: nQ
  RS_FF rs_ff_18 (.S(and_17_out[1]), .C(gcore_clk), .R(and_2_out), .Q(rs_ff_17_q[1]));  // open: nQ
  RS_FF rs_ff_19 (.S(and_17_out[2]), .C(gcore_clk), .R(and_2_out), .Q(rs_ff_17_q[2]));  // open: nQ
  RS_FF rs_ff_20 (.S(and_17_out[3]), .C(gcore_clk), .R(and_2_out), .Q(rs_ff_17_q[3]));  // open: nQ
  RS_FF rs_ff_21 (.S(and_17_out[4]), .C(gcore_clk), .R(and_2_out), .Q(rs_ff_17_q[4]));  // open: nQ
  RS_FF rs_ff_22 (.S(and_17_out[5]), .C(gcore_clk), .R(and_2_out), .Q(rs_ff_17_q[5]));  // open: nQ
  RS_FF rs_ff_23 (.S(and_17_out[6]), .C(gcore_clk), .R(and_2_out), .Q(rs_ff_17_q[6]));  // open: nQ
  RS_FF rs_ff_24 (.S(and_17_out[7]), .C(gcore_clk), .R(and_2_out), .Q(rs_ff_17_q[7]));  // open: nQ
  RS_FF rs_ff_25 (.S(and_17_out[8]), .C(gcore_clk), .R(and_2_out), .Q(rs_ff_17_q[8]));  // open: nQ
  RS_FF rs_ff_26 (.S(and_17_out[9]), .C(gcore_clk), .R(and_2_out), .Q(rs_ff_17_q[9]));  // open: nQ
  RS_FF rs_ff_27 (.S(and_17_out[10]), .C(gcore_clk), .R(and_2_out), .Q(rs_ff_17_q[10]));  // open: nQ
  RS_FF rs_ff_28 (.S(and_17_out[11]), .C(gcore_clk), .R(and_2_out), .Q(rs_ff_17_q[11]));  // open: nQ
  RS_FF rs_ff_29 (.S(and_17_out[12]), .C(gcore_clk), .R(and_2_out), .Q(rs_ff_17_q[12]));  // open: nQ
  RS_FF rs_ff_30 (.S(and_17_out[13]), .C(gcore_clk), .R(and_2_out), .Q(rs_ff_17_q[13]));  // open: nQ
  RS_FF rs_ff_31 (.S(and_17_out[14]), .C(gcore_clk), .R(and_2_out), .Q(rs_ff_17_q[14]));  // open: nQ
  LED led_10 (.in(rs_ff_9_q));
  LED led_11 (.in(rs_ff_10_q));
  LED led_12 (.in(rs_ff_11_q));
  LED led_13 (.in(rs_ff_12_q));
  LED led_14 (.in(rs_ff_13_q));
  LED led_15 (.in(rs_ff_14_q));
  LED led_16 (.in(rs_ff_15_q));
  LED led_17 (.in(rs_ff_16_q));
  assign driver_1_out = undriven ? rs_ff_9_q : 1'bz;  // Driver driver_9
  assign driver_1_out = undriven_2 ? rs_ff_10_q : 1'bz;  // Driver driver_10
  assign driver_1_out = undriven_3 ? rs_ff_11_q : 1'bz;  // Driver driver_11
  assign driver_1_out = undriven_4 ? rs_ff_12_q : 1'bz;  // Driver driver_12
  assign driver_1_out = undriven_5 ? rs_ff_13_q : 1'bz;  // Driver driver_13
  assign driver_1_out = undriven_6 ? rs_ff_14_q : 1'bz;  // Driver driver_14
  assign driver_1_out = undriven_7 ? rs_ff_15_q : 1'bz;  // Driver driver_15
  assign driver_1_out = undriven_8 ? rs_ff_16_q : 1'bz;  // Driver driver_16
  and and_26 (and_26_out, and_50_out, and_66_out[5]);
  and and_27 (and_27_out, and_51_out, and_66_out[5]);
  and and_28 (and_28_out, and_52_out, and_66_out[5]);
  and and_29 (and_29_out, and_53_out, and_66_out[5]);
  and and_30 (and_30_out, and_54_out, and_66_out[5]);
  and and_31 (and_31_out, and_55_out, and_66_out[5]);
  and and_32 (and_32_out, and_56_out, and_66_out[5]);
  and and_33 (and_33_out, and_57_out, and_66_out[5]);
  RS_FF rs_ff_32 (.S(and_26_out), .C(gcore_clk), .R(and_2_out), .Q(rs_ff_32_q));  // open: nQ
  RS_FF rs_ff_33 (.S(and_27_out), .C(gcore_clk), .R(and_2_out), .Q(rs_ff_33_q));  // open: nQ
  RS_FF rs_ff_34 (.S(and_28_out), .C(gcore_clk), .R(and_2_out), .Q(rs_ff_34_q));  // open: nQ
  RS_FF rs_ff_35 (.S(and_29_out), .C(gcore_clk), .R(and_2_out), .Q(rs_ff_35_q));  // open: nQ
  RS_FF rs_ff_36 (.S(and_30_out), .C(gcore_clk), .R(and_2_out), .Q(rs_ff_36_q));  // open: nQ
  RS_FF rs_ff_37 (.S(and_31_out), .C(gcore_clk), .R(and_2_out), .Q(rs_ff_37_q));  // open: nQ
  RS_FF rs_ff_38 (.S(and_32_out), .C(gcore_clk), .R(and_2_out), .Q(rs_ff_38_q));  // open: nQ
  RS_FF rs_ff_39 (.S(and_33_out), .C(gcore_clk), .R(and_2_out), .Q(rs_ff_39_q));  // open: nQ
  LED led_18 (.in(rs_ff_32_q));
  LED led_19 (.in(rs_ff_33_q));
  LED led_20 (.in(rs_ff_34_q));
  LED led_21 (.in(rs_ff_35_q));
  LED led_22 (.in(rs_ff_36_q));
  LED led_23 (.in(rs_ff_37_q));
  LED led_24 (.in(rs_ff_38_q));
  LED led_25 (.in(rs_ff_39_q));
  assign driver_1_out = undriven_9 ? rs_ff_32_q : 1'bz;  // Driver driver_17
  assign driver_1_out = undriven_10 ? rs_ff_33_q : 1'bz;  // Driver driver_18
  assign driver_1_out = undriven_11 ? rs_ff_34_q : 1'bz;  // Driver driver_19
  assign driver_1_out = undriven_12 ? rs_ff_35_q : 1'bz;  // Driver driver_20
  assign driver_1_out = undriven_13 ? rs_ff_36_q : 1'bz;  // Driver driver_21
  assign driver_1_out = undriven_14 ? rs_ff_37_q : 1'bz;  // Driver driver_22
  assign driver_1_out = undriven_15 ? rs_ff_38_q : 1'bz;  // Driver driver_23
  assign driver_1_out = undriven_16 ? rs_ff_39_q : 1'bz;  // Driver driver_24
  and and_34 (and_34_out, and_50_out, and_66_out[4]);
  and and_35 (and_35_out, and_51_out, and_66_out[4]);
  and and_36 (and_36_out, and_52_out, and_66_out[4]);
  and and_37 (and_37_out, and_53_out, and_66_out[4]);
  and and_38 (and_38_out, and_54_out, and_66_out[4]);
  and and_39 (and_39_out, and_55_out, and_66_out[4]);
  and and_40 (and_40_out, and_56_out, and_66_out[4]);
  and and_41 (and_41_out, and_57_out, and_66_out[4]);
  RS_FF rs_ff_40 (.S(and_34_out), .C(gcore_clk), .R(and_2_out), .Q(rs_ff_40_q));  // open: nQ
  RS_FF rs_ff_41 (.S(and_35_out), .C(gcore_clk), .R(and_2_out), .Q(rs_ff_41_q));  // open: nQ
  RS_FF rs_ff_42 (.S(and_36_out), .C(gcore_clk), .R(and_2_out), .Q(rs_ff_42_q));  // open: nQ
  RS_FF rs_ff_43 (.S(and_37_out), .C(gcore_clk), .R(and_2_out), .Q(rs_ff_43_q));  // open: nQ
  RS_FF rs_ff_44 (.S(and_38_out), .C(gcore_clk), .R(and_2_out), .Q(rs_ff_44_q));  // open: nQ
  RS_FF rs_ff_45 (.S(and_39_out), .C(gcore_clk), .R(and_2_out), .Q(rs_ff_45_q));  // open: nQ
  RS_FF rs_ff_46 (.S(and_40_out), .C(gcore_clk), .R(and_2_out), .Q(rs_ff_46_q));  // open: nQ
  RS_FF rs_ff_47 (.S(and_41_out), .C(gcore_clk), .R(and_2_out), .Q(rs_ff_47_q));  // open: nQ
  LED led_26 (.in(rs_ff_40_q));
  assign driver_1_out = undriven_17 ? rs_ff_40_q : 1'bz;  // Driver driver_25
  LED led_27 (.in(rs_ff_41_q));
  assign driver_1_out = undriven_18 ? rs_ff_41_q : 1'bz;  // Driver driver_26
  LED led_28 (.in(rs_ff_42_q));
  assign driver_1_out = undriven_19 ? rs_ff_42_q : 1'bz;  // Driver driver_27
  LED led_29 (.in(rs_ff_43_q));
  assign driver_1_out = undriven_20 ? rs_ff_43_q : 1'bz;  // Driver driver_28
  LED led_30 (.in(rs_ff_44_q));
  assign driver_1_out = undriven_21 ? rs_ff_44_q : 1'bz;  // Driver driver_29
  LED led_31 (.in(rs_ff_45_q));
  assign driver_1_out = undriven_22 ? rs_ff_45_q : 1'bz;  // Driver driver_30
  LED led_32 (.in(rs_ff_46_q));
  assign driver_1_out = undriven_23 ? rs_ff_46_q : 1'bz;  // Driver driver_31
  LED led_33 (.in(rs_ff_47_q));
  assign driver_1_out = undriven_24 ? rs_ff_47_q : 1'bz;  // Driver driver_32
  and and_42 (and_42_out, ~gcore_data_in[14], ~gcore_data_in[13], ~gcore_data_in[12]);  // And
  and and_43 (and_43_out, ~gcore_data_in[14], ~gcore_data_in[13], gcore_data_in[12]);  // And
  and and_44 (and_44_out, ~gcore_data_in[14], gcore_data_in[13], ~gcore_data_in[12]);  // And
  and and_45 (and_45_out, ~gcore_data_in[14], gcore_data_in[13], gcore_data_in[12]);  // And
  and and_46 (and_46_out, gcore_data_in[14], ~gcore_data_in[13], ~gcore_data_in[12]);  // And
  and and_47 (and_47_out, gcore_data_in[14], ~gcore_data_in[13], gcore_data_in[12]);  // And
  and and_48 (and_48_out, gcore_data_in[14], gcore_data_in[13], ~gcore_data_in[12]);  // And
  and and_49 (and_49_out, gcore_data_in[14], gcore_data_in[13], gcore_data_in[12]);
  and and_50 (and_50_out, and_42_out, and_4_out[7]);
  and and_51 (and_51_out, and_43_out, and_4_out[7]);
  and and_52 (and_52_out, and_44_out, and_4_out[7]);
  and and_53 (and_53_out, and_45_out, and_4_out[7]);
  and and_54 (and_54_out, and_46_out, and_4_out[7]);
  and and_55 (and_55_out, and_47_out, and_4_out[7]);
  and and_56 (and_56_out, and_48_out, and_4_out[7]);
  and and_57 (and_57_out, and_49_out, and_4_out[7]);
  and and_58 (and_58_out, and_50_out, and_66_out[3]);
  and and_59 (and_59_out, and_51_out, and_66_out[3]);
  and and_60 (and_60_out, and_52_out, and_66_out[3]);
  and and_61 (and_61_out, and_53_out, and_66_out[3]);
  and and_62 (and_62_out, and_54_out, and_66_out[3]);
  and and_63 (and_63_out, and_55_out, and_66_out[3]);
  and and_64 (and_64_out, and_56_out, and_66_out[3]);
  and and_65 (and_65_out, and_57_out, and_66_out[3]);
  RS_FF rs_ff_48 (.S(and_58_out), .C(gcore_clk), .R(and_2_out), .Q(rs_ff_48_q));  // open: nQ
  RS_FF rs_ff_49 (.S(and_59_out), .C(gcore_clk), .R(and_2_out), .Q(rs_ff_49_q));  // open: nQ
  RS_FF rs_ff_50 (.S(and_60_out), .C(gcore_clk), .R(and_2_out), .Q(rs_ff_50_q));  // open: nQ
  RS_FF rs_ff_51 (.S(and_61_out), .C(gcore_clk), .R(and_2_out), .Q(rs_ff_51_q));  // open: nQ
  RS_FF rs_ff_52 (.S(and_62_out), .C(gcore_clk), .R(and_2_out), .Q(rs_ff_52_q));  // open: nQ
  RS_FF rs_ff_53 (.S(and_63_out), .C(gcore_clk), .R(and_2_out), .Q(rs_ff_53_q));  // open: nQ
  RS_FF rs_ff_54 (.S(and_64_out), .C(gcore_clk), .R(and_2_out), .Q(rs_ff_54_q));  // open: nQ
  RS_FF rs_ff_55 (.S(and_65_out), .C(gcore_clk), .R(and_2_out), .Q(rs_ff_55_q));  // open: nQ
  LED led_34 (.in(rs_ff_48_q));
  LED led_35 (.in(rs_ff_49_q));
  LED led_36 (.in(rs_ff_50_q));
  LED led_37 (.in(rs_ff_51_q));
  LED led_38 (.in(rs_ff_52_q));
  LED led_39 (.in(rs_ff_53_q));
  LED led_40 (.in(rs_ff_54_q));
  LED led_41 (.in(rs_ff_55_q));
  assign driver_1_out = undriven_25 ? rs_ff_48_q : 1'bz;  // Driver driver_33
  assign driver_1_out = undriven_26 ? rs_ff_49_q : 1'bz;  // Driver driver_34
  assign driver_1_out = undriven_27 ? rs_ff_50_q : 1'bz;  // Driver driver_35
  assign driver_1_out = undriven_28 ? rs_ff_51_q : 1'bz;  // Driver driver_36
  assign driver_1_out = undriven_29 ? rs_ff_52_q : 1'bz;  // Driver driver_37
  assign driver_1_out = undriven_30 ? rs_ff_53_q : 1'bz;  // Driver driver_38
  assign driver_1_out = undriven_31 ? rs_ff_54_q : 1'bz;  // Driver driver_39
  assign driver_1_out = undriven_32 ? rs_ff_55_q : 1'bz;  // Driver driver_40
  assign and_66_out = {8{and_4_out[7]}} & gcore_data_in[7:0];  // And and_66, 8 bits wide
  and and_67 (and_67_out, and_50_out, and_66_out[2]);
  and and_68 (and_68_out, and_51_out, and_66_out[2]);
  and and_69 (and_69_out, and_52_out, and_66_out[2]);
  and and_70 (and_70_out, and_53_out, and_66_out[2]);
  and and_71 (and_71_out, and_54_out, and_66_out[2]);
  and and_72 (and_72_out, and_55_out, and_66_out[2]);
  and and_73 (and_73_out, and_56_out, and_66_out[2]);
  and and_74 (and_74_out, and_57_out, and_66_out[2]);
  RS_FF_AS rs_ff_as_1 (.S(and_5_out), .R(and_79_out), .Q(rs_ff_as_1_q));  // open: nQ
  RS_FF rs_ff_56 (.S(and_67_out), .C(gcore_clk), .R(and_2_out), .Q(rs_ff_56_q));  // open: nQ
  RS_FF rs_ff_57 (.S(and_68_out), .C(gcore_clk), .R(and_2_out), .Q(rs_ff_57_q));  // open: nQ
  RS_FF rs_ff_58 (.S(and_69_out), .C(gcore_clk), .R(and_2_out), .Q(rs_ff_58_q));  // open: nQ
  RS_FF rs_ff_59 (.S(and_70_out), .C(gcore_clk), .R(and_2_out), .Q(rs_ff_59_q));  // open: nQ
  RS_FF rs_ff_60 (.S(and_71_out), .C(gcore_clk), .R(and_2_out), .Q(rs_ff_60_q));  // open: nQ
  RS_FF rs_ff_61 (.S(and_72_out), .C(gcore_clk), .R(and_2_out), .Q(rs_ff_61_q));  // open: nQ
  RS_FF rs_ff_62 (.S(and_73_out), .C(gcore_clk), .R(and_2_out), .Q(rs_ff_62_q));  // open: nQ
  RS_FF rs_ff_63 (.S(and_74_out), .C(gcore_clk), .R(and_2_out), .Q(rs_ff_63_q));  // open: nQ
  LED led_42 (.in(rs_ff_56_q));
  LED led_43 (.in(rs_ff_57_q));
  LED led_44 (.in(rs_ff_58_q));
  LED led_45 (.in(rs_ff_59_q));
  LED led_46 (.in(rs_ff_60_q));
  LED led_47 (.in(rs_ff_61_q));
  LED led_48 (.in(rs_ff_62_q));
  LED led_49 (.in(rs_ff_63_q));
  assign driver_1_out = undriven_33 ? rs_ff_56_q : 1'bz;  // Driver driver_41
  assign driver_1_out = undriven_34 ? rs_ff_57_q : 1'bz;  // Driver driver_42
  assign driver_1_out = undriven_35 ? rs_ff_58_q : 1'bz;  // Driver driver_43
  assign driver_1_out = undriven_36 ? rs_ff_59_q : 1'bz;  // Driver driver_44
  assign driver_1_out = undriven_37 ? rs_ff_60_q : 1'bz;  // Driver driver_45
  assign driver_1_out = undriven_38 ? rs_ff_61_q : 1'bz;  // Driver driver_46
  assign driver_1_out = undriven_39 ? rs_ff_62_q : 1'bz;  // Driver driver_47
  assign driver_1_out = undriven_40 ? rs_ff_63_q : 1'bz;  // Driver driver_48
  JK_FF jk_ff_1 (.J(rs_ff_as_1_q), .C(gcore_clk), .K(rs_ff_as_1_q), .Q(jk_ff_1_q));  // open: nQ
  JK_FF jk_ff_2 (.J(jk_ff_1_q), .C(gcore_clk), .K(jk_ff_1_q), .Q(jk_ff_2_q));  // open: nQ
  JK_FF jk_ff_3 (.J(and_75_out), .C(gcore_clk), .K(and_75_out), .Q(jk_ff_3_q));  // open: nQ
  JK_FF jk_ff_4 (.J(and_76_out), .C(gcore_clk), .K(and_76_out), .Q(jk_ff_4_q));  // open: nQ
  JK_FF jk_ff_5 (.J(and_77_out), .C(gcore_clk), .K(and_77_out), .Q(jk_ff_5_q));  // open: nQ
  JK_FF jk_ff_6 (.J(and_78_out), .C(gcore_clk), .K(and_78_out), .Q(jk_ff_6_q));  // open: nQ
  and and_75 (and_75_out, jk_ff_1_q, jk_ff_2_q);
  and and_76 (and_76_out, and_75_out, jk_ff_3_q);
  and and_77 (and_77_out, and_76_out, jk_ff_4_q);
  and and_78 (and_78_out, and_77_out, jk_ff_5_q);
  and and_79 (and_79_out, and_78_out, jk_ff_6_q);
  and and_80 (and_80_out, and_50_out, and_66_out[1]);
  and and_81 (and_81_out, and_51_out, and_66_out[1]);
  and and_82 (and_82_out, and_52_out, and_66_out[1]);
  and and_83 (and_83_out, and_53_out, and_66_out[1]);
  and and_84 (and_84_out, and_54_out, and_66_out[1]);
  and and_85 (and_85_out, and_55_out, and_66_out[1]);
  and and_86 (and_86_out, and_56_out, and_66_out[1]);
  and and_87 (and_87_out, and_57_out, and_66_out[1]);
  RS_FF rs_ff_64 (.S(and_80_out), .C(gcore_clk), .R(and_2_out), .Q(rs_ff_64_q));  // open: nQ
  RS_FF rs_ff_65 (.S(and_81_out), .C(gcore_clk), .R(and_2_out), .Q(rs_ff_65_q));  // open: nQ
  RS_FF rs_ff_66 (.S(and_82_out), .C(gcore_clk), .R(and_2_out), .Q(rs_ff_66_q));  // open: nQ
  RS_FF rs_ff_67 (.S(and_83_out), .C(gcore_clk), .R(and_2_out), .Q(rs_ff_67_q));  // open: nQ
  RS_FF rs_ff_68 (.S(and_84_out), .C(gcore_clk), .R(and_2_out), .Q(rs_ff_68_q));  // open: nQ
  RS_FF rs_ff_69 (.S(and_85_out), .C(gcore_clk), .R(and_2_out), .Q(rs_ff_69_q));  // open: nQ
  RS_FF rs_ff_70 (.S(and_86_out), .C(gcore_clk), .R(and_2_out), .Q(rs_ff_70_q));  // open: nQ
  RS_FF rs_ff_71 (.S(and_87_out), .C(gcore_clk), .R(and_2_out), .Q(rs_ff_71_q));  // open: nQ
  LED led_50 (.in(rs_ff_64_q));
  LED led_51 (.in(rs_ff_65_q));
  LED led_52 (.in(rs_ff_66_q));
  LED led_53 (.in(rs_ff_67_q));
  LED led_54 (.in(rs_ff_68_q));
  LED led_55 (.in(rs_ff_69_q));
  LED led_56 (.in(rs_ff_70_q));
  LED led_57 (.in(rs_ff_71_q));
  assign driver_1_out = undriven_41 ? rs_ff_64_q : 1'bz;  // Driver driver_49
  assign driver_1_out = undriven_42 ? rs_ff_65_q : 1'bz;  // Driver driver_50
  assign driver_1_out = undriven_43 ? rs_ff_66_q : 1'bz;  // Driver driver_51
  assign driver_1_out = undriven_44 ? rs_ff_67_q : 1'bz;  // Driver driver_52
  assign driver_1_out = undriven_45 ? rs_ff_68_q : 1'bz;  // Driver driver_53
  assign driver_1_out = undriven_46 ? rs_ff_69_q : 1'bz;  // Driver driver_54
  assign driver_1_out = undriven_47 ? rs_ff_70_q : 1'bz;  // Driver driver_55
  assign driver_1_out = undriven_48 ? rs_ff_71_q : 1'bz;  // Driver driver_56
  and and_88 (and_88_out, and_50_out, and_66_out[0]);
  and and_89 (and_89_out, and_51_out, and_66_out[0]);
  and and_90 (and_90_out, and_52_out, and_66_out[0]);
  and and_91 (and_91_out, and_53_out, and_66_out[0]);
  and and_92 (and_92_out, and_54_out, and_66_out[0]);
  and and_93 (and_93_out, and_55_out, and_66_out[0]);
  and and_94 (and_94_out, and_56_out, and_66_out[0]);
  and and_95 (and_95_out, and_57_out, and_66_out[0]);
  RS_FF rs_ff_72 (.S(and_88_out), .C(gcore_clk), .R(and_2_out), .Q(rs_ff_72_q));  // open: nQ
  RS_FF rs_ff_73 (.S(and_89_out), .C(gcore_clk), .R(and_2_out), .Q(rs_ff_73_q));  // open: nQ
  RS_FF rs_ff_74 (.S(and_90_out), .C(gcore_clk), .R(and_2_out), .Q(rs_ff_74_q));  // open: nQ
  RS_FF rs_ff_75 (.S(and_91_out), .C(gcore_clk), .R(and_2_out), .Q(rs_ff_75_q));  // open: nQ
  RS_FF rs_ff_76 (.S(and_92_out), .C(gcore_clk), .R(and_2_out), .Q(rs_ff_76_q));  // open: nQ
  RS_FF rs_ff_77 (.S(and_93_out), .C(gcore_clk), .R(and_2_out), .Q(rs_ff_77_q));  // open: nQ
  RS_FF rs_ff_78 (.S(and_94_out), .C(gcore_clk), .R(and_2_out), .Q(rs_ff_78_q));  // open: nQ
  RS_FF rs_ff_79 (.S(and_95_out), .C(gcore_clk), .R(and_2_out), .Q(rs_ff_79_q));  // open: nQ
  LED led_58 (.in(rs_ff_72_q));
  assign driver_1_out = undriven_49 ? rs_ff_72_q : 1'bz;  // Driver driver_57
  LED led_59 (.in(rs_ff_73_q));
  assign driver_1_out = undriven_50 ? rs_ff_73_q : 1'bz;  // Driver driver_58
  LED led_60 (.in(rs_ff_74_q));
  assign driver_1_out = undriven_51 ? rs_ff_74_q : 1'bz;  // Driver driver_59
  LED led_61 (.in(rs_ff_75_q));
  assign driver_1_out = undriven_52 ? rs_ff_75_q : 1'bz;  // Driver driver_60
  LED led_62 (.in(rs_ff_76_q));
  assign driver_1_out = undriven_53 ? rs_ff_76_q : 1'bz;  // Driver driver_61
  LED led_63 (.in(rs_ff_77_q));
  assign driver_1_out = undriven_54 ? rs_ff_77_q : 1'bz;  // Driver driver_62
  LED led_64 (.in(rs_ff_78_q));
  assign driver_1_out = undriven_55 ? rs_ff_78_q : 1'bz;  // Driver driver_63
  LED led_65 (.in(rs_ff_79_q));
  assign driver_1_out = undriven_56 ? rs_ff_79_q : 1'bz;  // Driver driver_64

  // Notes on the sheet:
  //   reset-core
  //   store-base-addr
  //   store-sprite-row
  //   print-sprite
endmodule
