// Digital circuit pxcore.dig as structural Verilog
module pxcore (
  input  [14:0] pxcore_data_in,
  output [14:0] pxcore_data_out
);

  // Pins of 1 and 15 bits meet at pxcore_data_in

  assign pxcore_data_out[8] = pxcore_data_in[0];
endmodule
